# Fritzing sketch circuit (saved by Fritzing 0.9.3b)

parts:
  Adafruit_BNO055_and_BMP280_BFF1 = Adafruit BNO055 and BMP280 BFF [part_number=#5937]
  Raspberry_Pi_1 = Raspberry Pi 4 [part_number=RPI-4-b]
  Mod1 = Raspberry Pi Pico
  Composant1 = Motor Driver 1A Dual TB6612FNG
  DC_Mot_Enc1 = DC Motor with two-phase hall-encoder [part_number=VT-E-G25A-06-177E]
  J1 = Basic Servo
  LED1 = RGB LED (com. cathode, rbg) [package="5 mm [THT]"]
  S1 = Pushbutton [package="[SMD]"]
  S2 = Toggle Switch [package=THT]
  J2 = Piezo Speaker
  M1 = RPlidar A1M8 [package=THT]
  U1 = TRANSCHIPTC5747 [package=camera_sfv24r-2st_2]  # not connected
  BAT1 = Battery Holders [package=lipo-1100mAh]
  BAT2 = Battery Holders [package=lipo-1100mAh]
  BAT3 = Battery Holders [package=lipo-1100mAh]
  C1 = Electrolytic Capacitor [capacitance=1000μF package="1010 [SMD, electrolytic]"]
  C2 = Electrolytic Capacitor [capacitance=1000μF package="1010 [SMD, electrolytic]"]
  U2 = Voltage Regulator - 5V [package="DPak [SMD]"]
  C3 = Electrolytic Capacitor [capacitance=1000μF package="1010 [SMD, electrolytic]"]
  C4 = Electrolytic Capacitor [capacitance=1000μF package="1010 [SMD, electrolytic]"]
  U3 = Voltage Regulator - 5V [package="DPak [SMD]"]
  C5 = Electrolytic Capacitor [capacitance=1000μF package="1010 [SMD, electrolytic]"]
  C6 = Electrolytic Capacitor [capacitance=1000μF package="1010 [SMD, electrolytic]"]
  U4 = Voltage Regulator - 5V [package="DPak [SMD]"]

nets:
  N1: Adafruit_BNO055_and_BMP280_BFF1.SDA, Mod1.pin_24
  N2: Adafruit_BNO055_and_BMP280_BFF1.SCL, Mod1.pin_25
  N3: Raspberry_Pi_1.GPIO15, M1.pin7
  N4: Raspberry_Pi_1.GPIO14, M1.pin6
  GND: Raspberry_Pi_1.GND, Mod1.pin_3, Mod1.pin_8, Mod1.pin_18, Mod1.pin_23, Mod1.pin_26, Mod1.pin_28, Mod1.pin_33, Mod1.pin_38, J1.gnd, LED1.common_cathode, S1.Pin_3, S1.Pin_4, J2.pin1
  N5: Mod1.pin_1, J1.pulse
  N6: Mod1.pin_17, LED1.green_anode
  N7: Mod1.pin_19, LED1.red_anode
  N8: Mod1.pin_20, LED1.blue_anode
  N9: Mod1.pin_27, J2.pin2
  N10: Mod1.pin_29, Composant1.AIN2
  N11: Mod1.pin_31, Composant1.AIN1
  N12: Mod1.pin_32, Composant1.STBY
  N13: Mod1.pin_34, Composant1.PWMA
  N14: Composant1.A02, DC_Mot_Enc1.pin6
  N15: Composant1.A01, DC_Mot_Enc1.pin1
  N16: S2.L2, BAT3.-
  N17: BAT1.-, BAT2.+
  N18: BAT2.-, BAT3.+
  N19: C1.+, U2.input_voltage
  N20: C2.-, U2.GND
  N21: C2.+, U2.output_voltage
  N22: C3.-, U3.GND
  N23: C3.+, U3.output_voltage
  N24: C4.+, U3.input_voltage
  N25: C5.-, U4.GND
  N26: C5.+, U4.output_voltage
  N27: C6.+, U4.input_voltage

custom parts:
  Adafruit BNO055 and BMP280 BFF: Our QT Py boards are a great way to make very small microcontroller projects that pack a ton of power - and now we have a way for you to turn many QT Py boards into powerful 9 degree-of-freedom (9DoF) motion plus pressure/altitude sensing projects that are super small! We call this the Adafruit BNO055 + BMP280 BFF—a "Best Friend Forever." When you were a kid, you may have learned about the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
  Raspberry Pi 4: The RPi4, a faster version of the awesome Raspberry Pi 2 B ARM Board with 40 pin gpio. Ready for special Raspberry Pi B+ and RPi2 Hat (Hardware attached (on) top)
  Raspberry Pi Pico: Raspberry Pi Pico. Based around the RP2040 microcontroller the Pico is a low cost microcontroller device bringing Raspberry Pi quality, cost, and easy of use to the microcontroller space. Jan 2021, Split part in to two versions: SMD (this one) and tht. This one is single sided and uses the castellation pads to solder the module to the board (no holes, other than for the USB connector!). The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
  RPlidar A1M8: .The RPLIDAR A1 is the next generation low cost 360 degree 2D laser scanner (LIDAR) solution developed by SLAMTEC. It can take up to 4000 samples of laser ranging per second with high rotation speed. And equipped with SLAMTEC patented OPTMAG technology, it breakouts the life limitation of traditional LIDAR system so as to work stably for a long time.
